# Fritzing sketch schema_be_cpp (saved by Fritzing 0.9.6b)
breadboards: 1

parts:
  LED1 = LED - 5mm [color="Red (633nm)" current=0.030 package="5 mm [THT]"]
  J1 = Piezo Speaker
  R1 = Resistor [tolerance=±5% power=0.25 resistance=220 package=THT]
  Grove1 = Grove OLED 128x96
  Grove2 = Grove Temperature Sensor
  Grove3 = Grove 3 Axis Digital Accelerometer 16g
  selectButton = Pushbutton [package="[THT]"]
  onOffButton = Pushbutton [package="[SMD]"]
  downButton = Pushbutton [package="[THT]"]
  upButton = Pushbutton [package="[THT]"]
  WeMos_D1_R1 = WeMos_D1_R2
  R2 = Resistor [tolerance=±5% power=0.25 resistance=220 package=THT]
  R3 = Resistor [tolerance=±5% power=0.25 resistance=220 package=THT]
  R4 = Resistor [tolerance=±5% power=0.25 resistance=220 package=THT]
  R5 = Resistor [tolerance=±5% power=0.25 resistance=220 package=THT]

nets:
  N1: LED1.cathode, R1.Pin_1
  GND: LED1.anode, J1.pin1, Grove1.GND, Grove2.GND, Grove3.GND, WeMos_D1_R1.connector21, R2.Pin_0, R3.Pin_0, R4.Pin_0, R5.Pin_0
  N2: J1.pin2, WeMos_D1_R1.connector2
  N3: R1.Pin_0, WeMos_D1_R1.connector9
  VCC: Grove1.VCC, Grove2.VCC, Grove3.VCC, selectButton.Pin_1, selectButton.Pin_2, onOffButton.Pin_1, onOffButton.Pin_2, downButton.Pin_1, downButton.Pin_2, upButton.Pin_1, upButton.Pin_2, WeMos_D1_R1.connector23
  N4: Grove1.SDA, WeMos_D1_R1.connector16
  N5: Grove1.SCL, WeMos_D1_R1.connector17
  N6: Grove2.SIG, WeMos_D1_R1.connector18
  N7: Grove3.SDA, WeMos_D1_R1.connector4
  N8: Grove3.SCL, WeMos_D1_R1.connector3
  N9: selectButton.Pin_3, selectButton.Pin_4, WeMos_D1_R1.connector12, R3.Pin_1
  N10: onOffButton.Pin_3, onOffButton.Pin_4
  N11: downButton.Pin_3, downButton.Pin_4, WeMos_D1_R1.connector11, R4.Pin_1
  N12: upButton.Pin_3, upButton.Pin_4, WeMos_D1_R1.connector13, R2.Pin_1
